# Fritzing sketch DHT11_HC-SR04_MLX90614 (saved by Fritzing 0.9.3b)
breadboards: 1

parts:
  ESP32_-_Back1 = ESP32 - CAM
  hc-sr1 = hc-sr04
  DHT1 = DHT11 Humitidy and Temperature Sensor
  U1 = MLX90614 [package=to-39]

nets:
  N1: ESP32_-_Back1.GPIO2, hc-sr1.Echo
  N2: ESP32_-_Back1.GPIO14, U1.PWM_SDA
  N3: ESP32_-_Back1.GPIO15, U1.SCL_VZ
  N4: ESP32_-_Back1.GPIO13, hc-sr1.Trig
  N5: ESP32_-_Back1.GPIO12, DHT1.DATA
  GND: ESP32_-_Back1.GND, hc-sr1.GND, DHT1.GND, U1.VSS
  VDD: ESP32_-_Back1.5V, hc-sr1.VCC, DHT1.VDD, U1.VDD

custom parts:
  ESP32 - CAM: The ESP32-CAM has a very competitive small-size camera module that can operate independently as a minimum system with a footprint of only 27*40.5*4.5mm and a deep sleep current of up to 6mA.
  DHT11 Humitidy and Temperature Sensor: DHT11 Humidity and Temperature Sensor
