# Fritzing sketch reconocimientoVazLele (saved by Fritzing 0.9.3b)
breadboards: 1

parts:
  Raspberry_Pi_1 = Raspberry Pi 4 [part_number=RPI-4-b]
  KY-1 = Keyes Relay [package=THT]
  KY-2 = Keyes Relay [package=THT]
  KY-3 = Keyes Relay [package=THT]
  KY-4 = Keyes Relay [package=THT]
  MIC2 = Microphone
  CONN2 = USB connector [package=THT]
  SP2 = SPEAKER [package=pcb_mount_speaker]
  TRRS2 = Audio Jack (TRRS) 3.5mm [part_number="LUMBERG JEITA RC-5325A" package="RC-5325A [SMD]"]

nets:
  N1: Raspberry_Pi_1.GPIO17, KY-1.signal
  N2: Raspberry_Pi_1.GPIO27, KY-2.signal
  N3: Raspberry_Pi_1.GPIO22, KY-4.signal
  N4: Raspberry_Pi_1.3V3, KY-3.signal
  N5: Raspberry_Pi_1.GND, KY-1.ground, KY-2.ground, KY-3.ground, KY-4.ground
  N6: Raspberry_Pi_1.5V, KY-1.power, KY-2.power, KY-3.power, KY-4.power
  N7: MIC2.pin2, CONN2.chassis5
  N8: SP2.+, TRRS2.TIP
  N9: SP2.-, TRRS2.SLEEVE

notes:
  Esquema de Raspberry pi 4 con actuadores para el control de accsesorios en casa

custom parts:
  Raspberry Pi 4: The RPi4, a faster version of the awesome Raspberry Pi 2 B ARM Board with 40 pin gpio. Ready for special Raspberry Pi B+ and RPi2 Hat (Hardware attached (on) top)
  Keyes Relay: The Keyes 5V relay module is suitable for SCM development, home appliance control. It uses a 5V~12V TIL control signal which can control DC / AC signal.
