# Fritzing sketch Control de sonido MP3 (saved by Fritzing 0.9.3b)
breadboards: 1

parts:
  DFPlayer_Mini1 = DFPlayer MINI [package="DIP (Dual Inline) [THT]"]
  Componente1 = Arduino Uno (Rev3)
  SP1 = SPEAKER [package=pcb_mount_speaker]
  R2 = Resistor [tolerance=±5% resistance=220 package="2010 [SMD]"]

nets:
  VCC: DFPlayer_Mini1.VCC, Componente1.5V
  N1: DFPlayer_Mini1.RX, R2.Pin_1
  N2: DFPlayer_Mini1.TX, Componente1.D10_PWM/SS
  N3: DFPlayer_Mini1.DAC_R, DFPlayer_Mini1.DAC_L, DFPlayer_Mini1.SPK1, DFPlayer_Mini1.GND#6, DFPlayer_Mini1.SPK2, Componente1.GND, SP1.+, SP1.-
  N4: DFPlayer_Mini1.IO_1, DFPlayer_Mini1.GND#9, DFPlayer_Mini1.IO_2, DFPlayer_Mini1.K1/ADC_KEY, DFPlayer_Mini1.K2/ADC_KEY
  N5: Componente1.D11_PWM/MOSI, R2.Pin_0

notes:
  Esquema de conección para control de sonido

custom parts:
  DFPlayer MINI: MP3 module by DFRobot.com for playing Music from an SD-Card. Supports WAV and MP3 files.
