# Fritzing sketch ReconocedordeVoz (saved by Fritzing 0.9.3b)
breadboards: 1

parts:
  Mod1 = elechouse_voice_recognition_module_v3
  Componente1 = Arduino Uno (Rev3)

nets:
  GND: Mod1.GND, Componente1.GND
  VCC: Mod1.VCC, Componente1.5V
  N1: Mod1.RXD, Componente1.D3_PWM
  N2: Mod1.TXD, Componente1.D2

notes:
  Diagrama de coneccion para reconocedor de voz

custom parts:
  elechouse_voice_recognition_module_v3: Elechouse voice recognition module v3. Module that accepts up to 7 voice commands via a microphone. Note: currently this part was made from a .png image of the board. Thus the pcb is probably not correctly dimensioned since the input data was not precise. Before making boards based on this part, print out the footprint and check it (and provide corrections via the Fritzing forums to correct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
