# Fritzing sketch controlRelevadores (saved by Fritzing 0.9.3b)
breadboards: 1

parts:
  Componente1 = Arduino Uno (Rev3)
  KY-1 = Keyes Relay [package=THT]
  KY-2 = Keyes Relay [package=THT]
  KY-3 = Keyes Relay [package=THT]

nets:
  N1: Componente1.D8, KY-1.signal
  N2: Componente1.D6_PWM, KY-2.signal
  N3: Componente1.D7, KY-3.signal
  N4: Componente1.5V, KY-1.power, KY-2.power, KY-3.power
  N5: KY-1.ground, KY-2.ground, KY-3.ground
  N6: KY-1.C, KY-1.NO

notes:
  Esquema de control de relevadores para encendido y apagado de componentes

custom parts:
  Keyes Relay: The Keyes 5V relay module is suitable for SCM development, home appliance control. It uses a 5V~12V TIL control signal which can control DC / AC signal.
