# Fritzing sketch reconocimeintodeVozSonidoControldeRelevadoresDIAGRAMACOMPLETO (saved by Fritzing 0.9.3b)
breadboards: 1

parts:
  Mod1 = elechouse_voice_recognition_module_v3
  DFPlayer_Mini1 = DFPlayer MINI [package="DIP (Dual Inline) [THT]"]
  KY-1 = Keyes Relay [package=THT]
  KY-2 = Keyes Relay [package=THT]
  KY-3 = Keyes Relay [package=THT]
  Componente1 = Arduino Uno (Rev3)
  J1 = Piezo Speaker
  R1 = Resistor [tolerance=±5% resistance=220 package="0805 [SMD]"]

nets:
  GND: Mod1.GND, DFPlayer_Mini1.GND#6, KY-1.ground, KY-3.ground, Componente1.GND
  VCC: Mod1.VCC, DFPlayer_Mini1.VCC, KY-1.power, KY-2.power, KY-3.power, Componente1.5V
  N1: Mod1.RXD, Componente1.D3_PWM
  N2: Mod1.TXD, Componente1.D2
  N3: DFPlayer_Mini1.RX, R1.Pin_1
  N4: DFPlayer_Mini1.TX, Componente1.D10_PWM/SS
  N5: DFPlayer_Mini1.SPK1, J1.pin2
  N6: DFPlayer_Mini1.SPK2, J1.pin1
  N7: KY-1.signal, Componente1.D8
  N8: KY-2.signal, Componente1.D7
  N9: KY-3.signal, Componente1.D6_PWM
  N10: Componente1.D11_PWM/MOSI, R1.Pin_0

notes:
  Diagrama de sistema de reconocimiento de voz y control de actuadores

custom parts:
  elechouse_voice_recognition_module_v3: Elechouse voice recognition module v3. Module that accepts up to 7 voice commands via a microphone. Note: currently this part was made from a .png image of the board. Thus the pcb is probably not correctly dimensioned since the input data was not precise. Before making boards based on this part, print out the footprint and check it (and provide corrections via the Fritzing forums to correct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
  DFPlayer MINI: MP3 module by DFRobot.com for playing Music from an SD-Card. Supports WAV and MP3 files.
  Keyes Relay: The Keyes 5V relay module is suitable for SCM development, home appliance control. It uses a 5V~12V TIL control signal which can control DC / AC signal.
